// Logisim project ex4.circ as structural Verilog: 1 circuit, main circuit Split
module Split (
  input  [7:0] In1,
  output Out1,
  output [7:0] Out2
);

  and and_1 (Out1, In1[0], In1[6]);
  not not_1 (Out2[0], Out1);
  // Pins of 1 and 3 bits meet at In1[2:0]
  // Pins of 1 and 2 bits meet at In1[7:6]
  // Pins of 1 and 8 bits meet at Out2

  // Notes on the sheet:
  //   PUT CIRCUITRY HERE
endmodule
